// Logisim project schemes.circ as structural Verilog: 1 circuit, main circuit DataPath
module DataPath (
  input  in_1,
  input  in_2,
  input  in_3,
  input  R1,
  input  PC,
  input  in_6,
  input  in_7,
  input  in_8,
  input  R2,
  input  SP,
  input  in_11,
  input  in_12,
  input  R3,
  input  R8,
  input  R4,
  input  R9,
  input  in_17,
  input  in_18,
  input  R5,
  input  R10,
  input  in_21,
  input  R6,
  input  R11,
  input  in_24,
  input  R12,
  input  in_26,
  input  in_27,
  input  in_28,
  input  in_29,
  input  [3:0] in_30,
  input  in_31,
  input  [2:0] in_32,
  input  in_33,
  output [31:0] out_34,
  output [2:0] out_35
);

  wire and_1_out, and_2_out, and_4_out, demultiplexer_1_out0, demultiplexer_1_out1, demultiplexer_2_out0,
       demultiplexer_2_out1, demultiplexer_2_out2, demultiplexer_2_out3, or_1_out;
  wire [2:0] comparator_1_lt;
  wire [31:0] adder_1_out, and_3_out, controlled_buffer_1_out, controlled_buffer_2_out, divider_1_out,
       multiplexer_1_out, multiplexer_2_out, multiplexer_3_out, multiplier_1_out, not_1_out, register_1_q,
       register_2_q, register_3_q, register_4_q, register_5_q, register_6_q, register_7_q, register_8_q,
       register_10_q, register_11_q, register_12_q, register_13_q, register_14_q, register_15_q,
       register_16_q, register_18_q, register_19_q, register_20_q, register_21_q, register_22_q,
       register_23_q, register_24_q, register_25_q, shifter_1_out, shifter_2_out;

  Register #(.width(32)) register_1 (.D(controlled_buffer_2_out), .Q(register_1_q), .clk(R1));  // open: en, clr
  Register #(.width(32)) register_2 (.D(controlled_buffer_2_out), .Q(register_2_q), .clk(R2));  // open: en, clr
  Register #(.width(32)) register_3 (.D(controlled_buffer_2_out), .Q(register_3_q), .clk(R3));  // open: en, clr
  Register #(.width(32)) register_4 (.D(controlled_buffer_2_out), .Q(register_4_q), .clk(R4));  // open: en, clr
  Register #(.width(32)) register_5 (.D(controlled_buffer_2_out), .Q(register_5_q), .clk(R5));  // open: en, clr
  Register #(.width(32)) register_6 (.D(controlled_buffer_2_out), .Q(register_6_q), .clk(R6));  // open: en, clr
  Register #(.width(32)) register_7 (.D(controlled_buffer_2_out), .Q(register_7_q), .clk(in_24));  // open: en, clr
  Register #(.width(32)) register_8 (.D(controlled_buffer_2_out), .Q(register_8_q), .clk(in_28));  // open: en, clr
  Register #(.width(32)) register_9 (.D(controlled_buffer_2_out), .Q(out_34), .clk(PC));  // open: en, clr
  Register #(.width(32)) register_10 (.D(controlled_buffer_2_out), .Q(register_10_q), .clk(SP));  // open: en, clr
  Register #(.width(32)) register_11 (.D(controlled_buffer_2_out), .Q(register_11_q), .clk(R8));  // open: en, clr
  Register #(.width(32)) register_12 (.D(controlled_buffer_2_out), .Q(register_12_q), .clk(R9));  // open: en, clr
  Register #(.width(32)) register_13 (.D(controlled_buffer_2_out), .Q(register_13_q), .clk(R10));  // open: en, clr
  Register #(.width(32)) register_14 (.D(controlled_buffer_2_out), .Q(register_14_q), .clk(R11));  // open: en, clr
  Register #(.width(32)) register_15 (.D(controlled_buffer_2_out), .Q(register_15_q), .clk(R12));  // open: en, clr
  Register #(.width(32)) register_16 (.D(controlled_buffer_2_out), .Q(register_16_q), .clk(in_29));  // open: en, clr
  Multiplexer #(.select(4), .width(32)) multiplexer_1 (
    .in0(register_1_q), .in1(register_2_q), .in2(register_3_q), .in3(register_4_q), .in4(out_34),
    .in5(register_10_q), .in6(register_11_q), .in7(register_12_q), .in8(register_13_q), .in9(register_14_q),
    .in10(register_15_q), .in11(register_16_q), .in12(register_5_q), .in13(register_6_q),
    .in14(register_7_q), .in15(register_8_q), .out(multiplexer_1_out), .sel(in_30));  // open: en
  Register #(.width(3)) register_17 (.D(comparator_1_lt), .Q(out_35), .clk(in_33));  // open: en, clr
  Register #(.width(32)) register_18 (
    .D(controlled_buffer_2_out), .Q(register_18_q), .clk(in_1), .clr(in_2));  // open: en
  Register #(.width(32)) register_19 (
    .D(controlled_buffer_2_out), .Q(register_19_q), .clk(in_11), .clr(in_12));  // open: en
  and and_1 (and_1_out, in_26, out_35[2]);
  Register #(.width(32)) register_20 (.D(multiplexer_1_out), .Q(register_20_q), .clk(in_17), .clr(in_18));  // open: en
  or or_1 (or_1_out, in_21, and_1_out);
  and and_2 (and_2_out, register_18_q[12], register_18_q[2], register_18_q[3], register_18_q[4], register_18_q[5], register_18_q[6], register_18_q[7], register_18_q[8], register_18_q[9], register_18_q[10], register_18_q[11], register_18_q[13], register_18_q[14], register_18_q[15], register_18_q[16], register_18_q[17], register_18_q[18], register_18_q[19], register_18_q[20], register_18_q[21], register_18_q[22], register_18_q[23]);
  Demultiplexer demultiplexer_1 (
    .out0(demultiplexer_1_out0), .out1(demultiplexer_1_out1), .in(in_3), .sel(and_2_out));  // open: en
  assign controlled_buffer_1_out = in_8 ? register_19_q : 32'bz;  // Controlled_Buffer controlled_buffer_1
  assign controlled_buffer_2_out = in_7 ? controlled_buffer_1_out : 32'bz;  // Controlled_Buffer controlled_buffer_2
  assign controlled_buffer_1_out = in_7 ? multiplexer_3_out : 32'bz;  // Controlled_Buffer controlled_buffer_3
  assign and_3_out = register_20_q & register_19_q;  // AND_Gate and_3, 32 bits wide
  assign not_1_out = ~register_19_q;  // NOT_Gate not_1, 32 bits wide
  Adder #(.width(32)) adder_1 (
    .a(register_20_q), .b(register_19_q), .out(adder_1_out), .cin(or_1_out), .cout(comparator_1_lt[2]));
  Shifter #(.width(32)) shifter_1 (.in(register_20_q), .\dist (register_19_q[4:0]), .out(shifter_1_out));
  Shifter #(.width(32), .shift("lr")) shifter_2 (.in(register_20_q), .\dist (register_19_q[4:0]), .out(shifter_2_out));
  Multiplier #(.width(32)) multiplier_1 (
    .a(register_20_q), .b(register_19_q), .out(multiplier_1_out));  // open: cin, cout
  Divider #(.width(32)) divider_1 (.a(register_20_q), .b(register_19_q), .out(divider_1_out));  // open: upper, rem
  RAM #(.addrWidth(24), .dataWidth(32)) ram_1 (
    .addr(register_18_q[23:0]), .data(controlled_buffer_1_out), .sel(demultiplexer_1_out0), .clk(in_6),
    .ld(in_7));  // open: clr
  and and_4 (and_4_out, in_6, demultiplexer_1_out1);
  Multiplexer #(.select(3), .width(32)) multiplexer_2 (
    .in0(and_3_out), .in1(not_1_out), .in2(adder_1_out), .in3(shifter_1_out), .in4(shifter_2_out),
    .in5({{16{1'b0}}, register_19_q[15:0]}), .in6(multiplier_1_out), .in7(divider_1_out),
    .out(multiplexer_2_out), .sel(in_32));  // open: en
  Demultiplexer #(.select(2)) demultiplexer_2 (
    .out0(demultiplexer_2_out0), .out1(demultiplexer_2_out1), .out2(demultiplexer_2_out2),
    .out3(demultiplexer_2_out3), .in(and_4_out), .sel(register_18_q[1:0]));  // open: en
  Comparator #(.width(32)) comparator_1 (
    .a(multiplexer_2_out), .b({32{1'b0}}), .eq(comparator_1_lt[1]), .lt(comparator_1_lt[0]));  // open: gt
  Register #(.width(32)) register_21 (.D(multiplexer_2_out), .Q(register_21_q), .clk(in_31));  // open: en, clr
  Register #(.width(32)) register_22 (
    .D(controlled_buffer_1_out), .Q(register_22_q), .clk(demultiplexer_2_out0));  // open: en, clr
  Register #(.width(32)) register_23 (
    .D(controlled_buffer_1_out), .Q(register_23_q), .clk(demultiplexer_2_out1));  // open: en, clr
  Register #(.width(32)) register_24 (
    .D(controlled_buffer_1_out), .Q(register_24_q), .clk(demultiplexer_2_out2));  // open: en, clr
  Register #(.width(32)) register_25 (
    .D(controlled_buffer_1_out), .Q(register_25_q), .clk(demultiplexer_2_out3));  // open: en, clr
  assign controlled_buffer_2_out = in_27 ? register_21_q : 32'bz;  // Controlled_Buffer controlled_buffer_4
  Multiplexer #(.select(2), .width(32)) multiplexer_3 (
    .in0(register_22_q), .in1(register_23_q), .in2(register_24_q), .in3(register_25_q),
    .out(multiplexer_3_out), .sel(register_18_q[1:0]));  // open: en

  // Notes on the sheet:
  //   R0
  //   R7
  //   IR
endmodule
